# Fritzing sketch Ton_Midi_Footswitch (saved by Fritzing 0.9.6b)
breadboards: 1

parts:
  Part1 = Arduino Leonardo (Rev3b)
  LED2 = LED - 3mm [color="Green (555nm)" current=0.030 package="3 mm [THT]"]
  LED3 = LED - 3mm [color="Blue (430nm)" current=0.030 package="3 mm [THT]"]
  R1 = Resistor [tolerance=±5% power=0.25 resistance=220 package=THT]
  R2 = Resistor [tolerance=±5% power=0.25 resistance=220 package=THT]
  R3 = Resistor [tolerance=±5% power=0.25 resistance=220 package=THT]
  R4 = Resistor [tolerance=±5% resistance=100 package="1206 [SMD]"]
  R5 = Resistor [tolerance=±5% resistance=100 package="1206 [SMD]"]
  R6 = Resistor [tolerance=±5% resistance=100 package="1206 [SMD]"]
  LED1 = LED - 3mm [color="Yellow (595nm)" current=0.030 package="3 mm [THT]"]
  S6 = Pushbutton [package="[THT]"]
  S2 = Pushbutton [package="[THT]"]
  S4 = Pushbutton [package="[THT]"]
  S5 = Pushbutton [package="[THT]"]
  S1 = Pushbutton [package="[THT]"]
  S3 = Pushbutton [package="[THT]"]
  LED4 = LED - 3mm [color="White (6500K)" current=0.030 package="3 mm [THT]"]
  LED5 = LED - 3mm [color="Red (635nm)" current=0.030 package="3 mm [THT]"]
  R7 = Resistor [tolerance=±5% power=0.25 resistance=220 package=THT]
  R8 = Resistor [tolerance=±5% power=0.25 resistance=220 package=THT]
  LED6 = RGB LED (com. anode, rbg) [package="5 mm [THT]"]

nets:
  N1: Part1.D2/SDA, S1.Pin_1, S1.Pin_2
  N2: Part1.D3_PWM/SCL, S3.Pin_1, S3.Pin_2
  N3: Part1.D4/A6, S2.Pin_1, S2.Pin_2
  N4: Part1.D5_PWM, S4.Pin_1, S4.Pin_2
  N5: Part1.D6_PWM/A7, S5.Pin_1, S5.Pin_2
  N6: Part1.D7, S6.Pin_1, S6.Pin_2
  N7: Part1.5V, LED6.common_anode
  N8: Part1.A1, R3.Pin_0
  N9: Part1.A2, R1.Pin_0
  N10: Part1.A3, R2.Pin_0
  N11: Part1.A4, R7.Pin_0
  N12: Part1.A5, R8.Pin_0
  N13: Part1.D9_PWM/A9, R4.Pin_1
  N14: Part1.D10_PWM/A10, R5.Pin_1
  N15: Part1.D11_PWM, R6.Pin_1
  N16: Part1.GND, LED2.cathode, LED3.cathode, LED1.cathode, S6.Pin_3, S6.Pin_4, S2.Pin_3, S2.Pin_4, S4.Pin_3, S4.Pin_4, S5.Pin_3, S5.Pin_4, S1.Pin_3, S1.Pin_4, S3.Pin_3, S3.Pin_4, LED4.cathode, LED5.cathode
  N17: LED2.anode, R7.Pin_1
  N18: LED3.anode, R8.Pin_1
  N19: R1.Pin_1, LED4.anode
  N20: R2.Pin_1, LED1.anode
  N21: R3.Pin_1, LED5.anode
  N22: R4.Pin_0, LED6.green_cathode
  N23: R5.Pin_0, LED6.blue_cathode
  N24: R6.Pin_0, LED6.red_cathode
